// Logisim project xor_from_nand.circ as structural Verilog: 1 circuit, main circuit main
module main (
  input  in_1,
  input  in_2,
  output out_3
);

  wire and_1_out, and_2_out, nand_1_out, nand_2_out, nand_3_out, nand_4_out;

  nand nand_1 (nand_1_out, in_2, in_2);
  nand nand_2 (nand_2_out, in_1, in_1);
  and and_1 (and_1_out, in_1, nand_1_out);
  and and_2 (and_2_out, nand_2_out, in_2);
  nand nand_3 (nand_3_out, and_1_out, and_1_out);
  nand nand_4 (nand_4_out, and_2_out, and_2_out);
  nand nand_5 (out_3, nand_3_out, nand_4_out);

  // Notes on the sheet:
  //   in_1: pull=up
  //   in_2: pull=up
endmodule
